# Fritzing sketch PHMeter (saved by Fritzing 0.9.9b)

parts:
  U1 = NodeMCU V1.0
  WATER_PUMP1 = water pump/motor
  WATER_PUMP2 = water pump/motor

nets:
  N1: U1.D5, WATER_PUMP2.pin_2
  N2: U1.D6, WATER_PUMP1.pin_2
  N3: U1.GND, WATER_PUMP1.pin_1, WATER_PUMP2.pin_1

custom parts:
  NodeMCU V1.0: ESP8266 based NodeMCU
  water pump/motor: WATER PUMP BY ARDUBLOCKTR
